# Fritzing sketch UsingTIP132 (saved by Fritzing 0.9.3b)

parts:
  Part2 = Arduino MicroSD Shield
  Q1 = npn-Powertransistor [package="TO220 [THT]"]

nets:
  N1: Part2.N$168, Q1.base
  N2: Part2.N$169, Q1.collector
  N3: Part2.N$170, Q1.emitter
